// Digital circuit ALU.dig as structural Verilog
module ALU (
  input  [31:0] A,
  input  [31:0] B,
  input  [3:0] Sel,
  output [31:0] R
);

  wire [0:0] slt_lt, sltu_lt;
  wire [31:0] add_1_s, and_1_out, multiplexer_1_out, or_1_out, shiftleft_1_out, shiftright_1_out, sub_1_s,
       xor_1_out;

  Add #(.Bits(32)) add_1 (.a(A), .b(B), .c_i(1'b0), .s(add_1_s));  // open: c_o
  Sub #(.Bits(32)) sub_1 (.a(A), .b(B), .c_i(1'b0), .s(sub_1_s));  // open: c_o
  ShiftLeft shiftleft_1 (.in(A), .shamt(B[4:0]), .out(shiftleft_1_out));
  Comparator #(.Signed("true"), .Bits(32)) slt (.a(A), .b(B), .lt(slt_lt[0]));  // open: gt, eq
  Comparator #(.Bits(32)) sltu (.a(A), .b(B), .lt(sltu_lt[0]));  // open: gt, eq
  assign xor_1_out = A ^ B;  // XOr xor_1, 32 bits wide
  ShiftRight shiftright_1 (.in(A), .shamt(B[4:0]), .arith(Sel[3]), .out(shiftright_1_out));
  assign or_1_out = A | B;  // Or or_1, 32 bits wide
  assign and_1_out = A & B;  // And and_1, 32 bits wide
  Multiplexer #(.Bits(32)) multiplexer_1 (.sel(Sel[3]), .in_0(add_1_s), .in_1(sub_1_s), .out(multiplexer_1_out));
  Multiplexer #(.Selector_Bits(3), .Bits(32)) multiplexer_2 (
    .sel(Sel[2:0]), .in_0(multiplexer_1_out), .in_1(shiftleft_1_out), .in_2({{31{1'b0}}, slt_lt[0]}),
    .in_3({{31{1'b0}}, sltu_lt[0]}), .in_4(xor_1_out), .in_5(shiftright_1_out), .in_6(or_1_out),
    .in_7(and_1_out), .out(R));

  // Other names for the same wires on the sheet: shamt[4:0] = B[4:0]; alt = Sel[3]
endmodule

/* Test case ALU:
A B Sel R
0x00000000 0x00000000 0 0x00000000
0x00000001 0x00000001 0 0x00000002
0xFFFFFFFF 0x00000001 0 0x00000000
0x00000001 0xFFFFFFFF 0 0x00000000
0x80000000 0x7FFFFFFF 0 0xFFFFFFFF
0x7FFFFFFF 0x80000000 0 0xFFFFFFFF
0x80000000 0x0000001F 0 0x8000001F
0x80000000 0x00000020 0 0x80000020
0xFFFFFFFF 0xFFFFFFFF 0 0xFFFFFFFE
0x12345678 0x00000004 0 0x1234567C
0x87654321 0x0000001C 0 0x8765433D
0x80000000 0x80000000 0 0x00000000
0x00000005 0xFFFFFFFB 0 0x00000000
0xFFFFFFFB 0x00000005 0 0x00000000
0xCE6F2A67 0x00000019 0 0xCE6F2A80
0xFD192565 0x56AC493D 0 0x53C56EA2
0xFFFFFFEF 0x0000001C 0 0x0000000B
0x00000002 0xF0A63899 0 0xF0A6389B
0x0000001E 0x622394AE 0 0x622394CC
0xFFFF0000 0x9E00C3E0 0 0x9DFFC3E0
0x00000000 0x00000011 0 0x00000011
0xB3E39CFF 0xFFFF0000 0 0xB3E29CFF
0x00000004 0x00000000 0 0x00000004
0x00000021 0x27BA72E0 0 0x27BA7301
0xB96DC437 0xFFFFFFE1 0 0xB96DC418
0x00000017 0xFFFFFFEC 0 0x00000003
0x00000000 0x00000000 8 0x00000000
0x00000001 0x00000001 8 0x00000000
0xFFFFFFFF 0x00000001 8 0xFFFFFFFE
0x00000001 0xFFFFFFFF 8 0x00000002
0x80000000 0x7FFFFFFF 8 0x00000001
0x7FFFFFFF 0x80000000 8 0xFFFFFFFF
0x80000000 0x0000001F 8 0x7FFFFFE1
0x80000000 0x00000020 8 0x7FFFFFE0
0xFFFFFFFF 0xFFFFFFFF 8 0x00000000
0x12345678 0x00000004 8 0x12345674
0x87654321 0x0000001C 8 0x87654305
0x80000000 0x80000000 8 0x00000000
0x00000005 0xFFFFFFFB 8 0x0000000A
0xFFFFFFFB 0x00000005 8 0xFFFFFFF6
0xFFFFFFEE 0xB2E7CBB5 8 0x4D183439
0x00000002 0xD8EA37F8 8 0x2715C80A
0x2F37E36C 0x7FFFFFFF 8 0xAF37E36D
0x8EAE3F93 0xBAB46A98 8 0xD3F9D4FB
0x6A9E0B67 0x8CFCB314 8 0xDDA15853
0xF37D992C 0x87654321 8 0x6C18560B
0x4FCE84D7 0x00000020 8 0x4FCE84B7
0xFFFFFFED 0x1E98C605 8 0xE16739E8
0xFFFFFFFE 0x896566A3 8 0x769A995B
0x00000002 0x0000001F 8 0xFFFFFFE3
0x00000011 0xC08AA97E 8 0x3F755693
0x33545E2F 0x87654321 8 0xABEF1B0E
0x00000000 0x00000000 1 0x00000000
0x00000001 0x00000001 1 0x00000002
0xFFFFFFFF 0x00000001 1 0xFFFFFFFE
0x00000001 0xFFFFFFFF 1 0x80000000
0x80000000 0x7FFFFFFF 1 0x00000000
0x7FFFFFFF 0x80000000 1 0x7FFFFFFF
0x80000000 0x0000001F 1 0x00000000
0x80000000 0x00000020 1 0x80000000
0xFFFFFFFF 0xFFFFFFFF 1 0x80000000
0x12345678 0x00000004 1 0x23456780
0x87654321 0x0000001C 1 0x10000000
0x80000000 0x80000000 1 0x80000000
0x00000005 0xFFFFFFFB 1 0x28000000
0xFFFFFFFB 0x00000005 1 0xFFFFFF60
0x186A2919 0xA56CC220 1 0x186A2919
0x12345678 0x00000007 1 0x1A2B3C00
0x497CC541 0xB1038F3B 1 0x08000000
0xE9122AF6 0x00000008 1 0x122AF600
0x87654321 0x0000FFFF 1 0x80000000
0x03AA54BD 0x87654321 1 0x0754A97A
0xFFFFFFE1 0x00000001 1 0xFFFFFFC2
0xD4A5577C 0x60F999FC 1 0xC0000000
0x00000001 0x0000001E 1 0x40000000
0x00000007 0xABAE9A05 1 0x000000E0
0xA493C8D6 0x00000000 1 0xA493C8D6
0x8BFEF0E0 0x00000018 1 0xE0000000
0x00000000 0x00000000 2 0x00000000
0x00000001 0x00000001 2 0x00000000
0xFFFFFFFF 0x00000001 2 0x00000001
0x00000001 0xFFFFFFFF 2 0x00000000
0x80000000 0x7FFFFFFF 2 0x00000001
0x7FFFFFFF 0x80000000 2 0x00000000
0x80000000 0x0000001F 2 0x00000001
0x80000000 0x00000020 2 0x00000001
0xFFFFFFFF 0xFFFFFFFF 2 0x00000000
0x12345678 0x00000004 2 0x00000000
0x87654321 0x0000001C 2 0x00000001
0x80000000 0x80000000 2 0x00000000
0x00000005 0xFFFFFFFB 2 0x00000000
0xFFFFFFFB 0x00000005 2 0x00000001
0x00000021 0x00000006 2 0x00000000
0x00000005 0xFFFFFFF9 2 0x00000000
0x55555555 0xEEACC635 2 0x00000000
0x19C7D3B2 0x0B812269 2 0x00000000
0xCDA84E9C 0x00000021 2 0x00000001
0x3A5D2F52 0x00000002 2 0x00000000
0x11E3D1C6 0xFFFF0000 2 0x00000000
0x2F562F76 0x80000001 2 0x00000000
0x2CF65254 0x7A9756B0 2 0x00000001
0xFFFFFFE9 0xFFFFFFEE 2 0x00000001
0xB1E0CA82 0x43234C85 2 0x00000001
0x55555555 0x1E66CA04 2 0x00000000
0x00000000 0x00000000 3 0x00000000
0x00000001 0x00000001 3 0x00000000
0xFFFFFFFF 0x00000001 3 0x00000000
0x00000001 0xFFFFFFFF 3 0x00000001
0x80000000 0x7FFFFFFF 3 0x00000000
0x7FFFFFFF 0x80000000 3 0x00000001
0x80000000 0x0000001F 3 0x00000000
0x80000000 0x00000020 3 0x00000000
0xFFFFFFFF 0xFFFFFFFF 3 0x00000000
0x12345678 0x00000004 3 0x00000000
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*/
