// Digital circuit BranchComp.dig as structural Verilog
module BranchComp (
  input  [31:0] A,
  input  [31:0] B,
  input  BrUn,
  output BrEq,
  output BrLT
);

  wire signed_lt, unsigned_lt;

  Comparator #(.Signed("true"), .Bits(32)) \signed  (.a(A), .b(B), .eq(BrEq), .lt(signed_lt));  // open: gt
  Comparator #(.Bits(32)) \unsigned  (.a(A), .b(B), .lt(unsigned_lt));  // open: gt, eq
  Multiplexer multiplexer_1 (.sel(BrUn), .in_0(signed_lt), .in_1(unsigned_lt), .out(BrLT));
endmodule

/* Test case BranchComp:
A B BrUn BrEq BrLT
0x00000000 0x00000000 0 1 0
0x00000000 0x00000000 1 1 0
0x00000001 0x00000000 0 0 0
0x00000001 0x00000000 1 0 0
0x00000000 0x00000001 0 0 1
0x00000000 0x00000001 1 0 1
0xFFFFFFFF 0x00000000 0 0 1
0xFFFFFFFF 0x00000000 1 0 0
0x00000000 0xFFFFFFFF 0 0 0
0x00000000 0xFFFFFFFF 1 0 1
0x80000000 0x7FFFFFFF 0 0 1
0x80000000 0x7FFFFFFF 1 0 0
0x7FFFFFFF 0x80000000 0 0 0
0x7FFFFFFF 0x80000000 1 0 1
0xFFFFFFFF 0xFFFFFFFF 0 1 0
0xFFFFFFFF 0xFFFFFFFF 1 1 0
0x80000000 0x80000000 0 1 0
0x80000000 0x80000000 1 1 0
0xFFFFFFFE 0xFFFFFFFF 0 0 1
0xFFFFFFFE 0xFFFFFFFF 1 0 1
0x00000005 0xFFFFFFFB 0 0 0
0x00000005 0xFFFFFFFB 1 0 1
0xFFFFFFE3 0xF2F229AB 0 0 0
0xFFFFFFE3 0xF2F229AB 1 0 0
0x543C2CA6 0x4E7D588E 0 0 0
0x543C2CA6 0x4E7D588E 1 0 0
0xFFFFFFE1 0xC835A8CC 0 0 0
0xFFFFFFE1 0xC835A8CC 1 0 0
0xF0D65CC3 0xB52168A2 0 0 0
0xF0D65CC3 0xB52168A2 1 0 0
0xA6BCB89D 0xAAAAAAAA 0 0 1
0xA6BCB89D 0xAAAAAAAA 1 0 1
0xFFFF0000 0xFFFFFFFA 0 0 1
0xFFFF0000 0xFFFFFFFA 1 0 1
0x00000001 0x1F720465 0 0 1
0x00000001 0x1F720465 1 0 1
0x00000014 0xFFFFFFFE 0 0 0
0x00000014 0xFFFFFFFE 1 0 1
0xFFFFFFE9 0xFFFFFFE4 0 0 0
0xFFFFFFE9 0xFFFFFFE4 1 0 0
0xFFFFFFFE 0x39B95D46 0 0 1
0xFFFFFFFE 0x39B95D46 1 0 0
0x00000020 0x00000002 0 0 0
0x00000020 0x00000002 1 0 0
0x0000001E 0x87654321 0 0 0
0x0000001E 0x87654321 1 0 1
0xFFFFFFFB 0x06DD6655 0 0 1
0xFFFFFFFB 0x06DD6655 1 0 0
0x00000001 0x87654321 0 0 0
0x00000001 0x87654321 1 0 1
0x22C07F1A 0x00000004 0 0 0
0x22C07F1A 0x00000004 1 0 0
0x93A407B6 0xD1FFAA2A 0 0 1
0x93A407B6 0xD1FFAA2A 1 0 1
0x00088ED5 0x00000010 0 0 0
0x00088ED5 0x00000010 1 0 0
0x7927B873 0x2F015646 0 0 0
0x7927B873 0x2F015646 1 0 0
0x376C2E9C 0x0000000D 0 0 0
0x376C2E9C 0x0000000D 1 0 0
0x00000006 0x80000001 0 0 0
0x00000006 0x80000001 1 0 1
0x2386F18A 0x00000015 0 0 0
0x2386F18A 0x00000015 1 0 0
0x21732068 0x3A5643FB 0 0 1
0x21732068 0x3A5643FB 1 0 1
0x0000FFFF 0xC40EDB4A 0 0 0
0x0000FFFF 0xC40EDB4A 1 0 1
0xFFFFFFFF 0xD8083F08 0 0 0
0xFFFFFFFF 0xD8083F08 1 0 0
0xFFFF0000 0x00000000 0 0 1
0xFFFF0000 0x00000000 1 0 0
0xADA38FCE 0x024FBA7C 0 0 1
0xADA38FCE 0x024FBA7C 1 0 0
0xFFFFFFFC 0x16C5362C 0 0 1
0xFFFFFFFC 0x16C5362C 1 0 0
0x0000001F 0x0000001E 0 0 0
0x0000001F 0x0000001E 1 0 0
0x55555555 0xFFFFFFF3 0 0 0
0x55555555 0xFFFFFFF3 1 0 1
0x00000001 0xD43AE417 0 0 0
0x00000001 0xD43AE417 1 0 1
*/
