// Digital circuit Control.dig as structural Verilog
module Control (
  input  [31:0] inst,
  input  BrEq,
  input  BrLT,
  output PCSel,
  output [2:0] ImmSel,
  output RegWEn,
  output BrUn,
  output ASel,
  output BSel,
  output [3:0] ALUSel,
  output MemRW,
  output [1:0] WBSel,
  output Halt
);

  wire and_11_out, and_12_out, and_13_out, c0, c1, c3, c4, c5, isAUIPC, isBRANCH, isJALR, isLOAD, isLUI,
       isOP, isOPIMM, multiplexer_1_out, or_1_out, or_8_out, r0, r1, r3, xor_1_out;

  Decoder #(.Selector_Bits(2)) decoder_1 (.sel(inst[6:5]), .out_0(r0), .out_1(r1), .out_3(r3));  // open: out_2
  Decoder #(.Selector_Bits(3)) decoder_2 (
    .sel(inst[4:2]), .out_0(c0), .out_1(c1), .out_3(c3), .out_4(c4), .out_5(c5));  // open: out_2, out_6, out_7
  and and_1 (isLOAD, r0, c0);
  and and_2 (isOPIMM, r0, c4);
  and and_3 (isAUIPC, r0, c5);
  and and_4 (MemRW, r1, c0);
  and and_5 (isOP, r1, c4);
  and and_6 (isLUI, r1, c5);
  and and_7 (isBRANCH, r3, c0);
  and and_8 (isJALR, r3, c1);
  and and_9 (ImmSel[2], r3, c3);
  and and_10 (Halt, r3, c4);
  Multiplexer multiplexer_1 (.sel(inst[14]), .in_0(BrEq), .in_1(BrLT), .out(multiplexer_1_out));
  or or_1 (or_1_out, isOP, isOPIMM);
  and and_11 (and_11_out, inst[14], ~inst[13], inst[12]);  // And
  xor xor_1 (xor_1_out, multiplexer_1_out, inst[12]);
  or or_2 (ImmSel[0], MemRW, isLUI, isAUIPC);
  or or_3 (ImmSel[1], isBRANCH, isLUI, isAUIPC);
  or or_4 (RegWEn, isOP, isOPIMM, isLOAD, ImmSel[2], isJALR, isLUI, isAUIPC);
  or or_5 (ASel, isBRANCH, ImmSel[2], isAUIPC);
  not not_1 (BSel, isOP);
  and and_12 (and_12_out, isOPIMM, and_11_out);
  or or_6 (WBSel[0], isLOAD, isLUI);
  or or_7 (WBSel[1], ImmSel[2], isJALR, isLUI);
  Multiplexer #(.Bits(3)) multiplexer_2 (.sel(or_1_out), .in_0(3'b000), .in_1(inst[14:12]), .out(ALUSel[2:0]));
  and and_13 (and_13_out, xor_1_out, isBRANCH);
  or or_8 (or_8_out, isOP, and_12_out);
  or or_9 (PCSel, ImmSel[2], isJALR, and_13_out);
  and and_14 (ALUSel[3], inst[30], or_8_out);

  assign BrUn = inst[13];

  // Other names for the same wires on the sheet: f3[2:0] = inst[14:12]; f3_0 = inst[12]; f3_1 = inst[13];
  //   f3_2 = inst[14]; i30 = inst[30]; isJAL = ImmSel[2]; isSTORE = MemRW; isSYSTEM = Halt
endmodule

/* Test case Control:
inst BrEq BrLT PCSel ImmSel RegWEn BrUn ASel BSel ALUSel MemRW WBSel Halt
0x01328033 1 0 0 x x x 0 0 0 0 0 0
0x608D8013 0 1 0 0 x x 0 1 0 0 0 0
0x39018013 1 0 0 0 x x 0 1 0 0 0 0
0x01601033 0 1 0 x x x 0 0 1 0 0 0
0x014C1013 0 0 0 0 x x 0 1 1 0 0 0
0x415ED013 1 0 0 0 x x 0 1 13 0 0 0
0x01592033 0 1 0 x x x 0 0 2 0 0 0
0xF0012013 0 0 0 0 x x 0 1 2 0 0 0
0x1088A013 1 1 0 0 x x 0 1 2 0 0 0
0x01963033 1 0 0 x x x 0 0 3 0 0 0
0xD7743013 1 0 0 0 x x 0 1 3 0 0 0
0x38153013 1 1 0 0 x x 0 1 3 0 0 0
0x0138C033 1 0 0 x x x 0 0 4 0 0 0
0x66BC4013 0 0 0 0 x x 0 1 4 0 0 0
0x3A63C013 0 0 0 0 x x 0 1 4 0 0 0
0x0137D033 1 0 0 x x x 0 0 5 0 0 0
0x01685013 1 0 0 0 x x 0 1 5 0 0 0
0x410B5013 0 1 0 0 x x 0 1 13 0 0 0
0x00366033 0 0 0 x x x 0 0 6 0 0 0
0x41EDE013 0 1 0 0 x x 0 1 6 0 0 0
0x082E6013 1 1 0 0 x x 0 1 6 0 0 0
0x01197033 0 1 0 x x x 0 0 7 0 0 0
0xC677F013 1 0 0 0 x x 0 1 7 0 0 0
0x00427013 1 0 0 0 x x 0 1 7 0 0 0
0x40868033 0 0 0 x x x 0 0 8 0 0 0
0x40565033 1 1 0 x x x 0 0 13 0 0 0
0xC9092003 1 1 0 0 x x 0 1 0 0 1 0
0xF8240067 0 0 1 0 x x 0 1 0 0 2 0
0x45640037 0 1 0 3 x x x x x 0 3 0
0xE3F11017 0 0 0 3 x x 1 1 0 0 0 0
0x0951406F 0 1 1 4 x x 1 1 0 0 2 0
0x00D780B3 1 0 0 x 1 x 0 0 0 0 0 0
0x4D608093 1 0 0 0 1 x 0 1 0 0 0 0
0x074F0093 1 1 0 0 1 x 0 1 0 0 0 0
0x007D90B3 1 1 0 x 1 x 0 0 1 0 0 0
0x01A51093 0 1 0 0 1 x 0 1 1 0 0 0
0x41B15093 1 0 0 0 1 x 0 1 13 0 0 0
0x00D120B3 0 0 0 x 1 x 0 0 2 0 0 0
0xC7D6A093 1 0 0 0 1 x 0 1 2 0 0 0
0x0402A093 0 0 0 0 1 x 0 1 2 0 0 0
0x006630B3 1 0 0 x 1 x 0 0 3 0 0 0
0x5EEAB093 0 0 0 0 1 x 0 1 3 0 0 0
0x351F3093 1 0 0 0 1 x 0 1 3 0 0 0
0x001C40B3 0 0 0 x 1 x 0 0 4 0 0 0
0x75124093 1 0 0 0 1 x 0 1 4 0 0 0
0x175A4093 1 0 0 0 1 x 0 1 4 0 0 0
0x01E0D0B3 0 0 0 x 1 x 0 0 5 0 0 0
0x0195D093 0 1 0 0 1 x 0 1 5 0 0 0
0x4129D093 0 0 0 0 1 x 0 1 13 0 0 0
0x00B9E0B3 0 1 0 x 1 x 0 0 6 0 0 0
0x69916093 1 0 0 0 1 x 0 1 6 0 0 0
0x24396093 0 1 0 0 1 x 0 1 6 0 0 0
0x0107F0B3 0 0 0 x 1 x 0 0 7 0 0 0
0xF2797093 1 1 0 0 1 x 0 1 7 0 0 0
0x10EB7093 0 1 0 0 1 x 0 1 7 0 0 0
0x41E800B3 1 0 0 x 1 x 0 0 8 0 0 0
0x40D3D0B3 1 0 0 x 1 x 0 0 13 0 0 0
0xA3862083 0 1 0 0 1 x 0 1 0 0 1 0
0x9F8900E7 1 1 1 0 1 x 0 1 0 0 2 0
0x5C2D20B7 0 0 0 3 1 x x x x 0 3 0
0x96C52097 0 1 0 3 1 x 1 1 0 0 0 0
0xEC3810EF 0 0 1 4 1 x 1 1 0 0 2 0
0x00890FB3 0 0 0 x 1 x 0 0 0 0 0 0
0xE45E8F93 0 1 0 0 1 x 0 1 0 0 0 0
0x20670F93 0 0 0 0 1 x 0 1 0 0 0 0
0x00229FB3 0 0 0 x 1 x 0 0 1 0 0 0
0x00EA9F93 0 1 0 0 1 x 0 1 1 0 0 0
0x41AB5F93 0 1 0 0 1 x 0 1 13 0 0 0
0x01A7AFB3 0 0 0 x 1 x 0 0 2 0 0 0
0xC63CAF93 0 0 0 0 1 x 0 1 2 0 0 0
0x1B19AF93 1 0 0 0 1 x 0 1 2 0 0 0
0x00E63FB3 0 1 0 x 1 x 0 0 3 0 0 0
0x50BD3F93 1 0 0 0 1 x 0 1 3 0 0 0
0x38953F93 0 0 0 0 1 x 0 1 3 0 0 0
0x0126CFB3 0 1 0 x 1 x 0 0 4 0 0 0
0x463FCF93 0 0 0 0 1 x 0 1 4 0 0 0
0x02424F93 1 1 0 0 1 x 0 1 4 0 0 0
0x01125FB3 1 1 0 x 1 x 0 0 5 0 0 0
0x0153DF93 0 1 0 0 1 x 0 1 5 0 0 0
0x4087DF93 1 0 0 0 1 x 0 1 13 0 0 0
0x000A6FB3 1 0 0 x 1 x 0 0 6 0 0 0
0x6A8EEF93 1 0 0 0 1 x 0 1 6 0 0 0
0x2A1AEF93 0 1 0 0 1 x 0 1 6 0 0 0
0x0151FFB3 1 1 0 x 1 x 0 0 7 0 0 0
0x59C2FF93 0 0 0 0 1 x 0 1 7 0 0 0
0x2F947F93 0 1 0 0 1 x 0 1 7 0 0 0
0x40BC0FB3 1 0 0 x 1 x 0 0 8 0 0 0
0x40CB5FB3 0 0 0 x 1 x 0 0 13 0 0 0
0x9821AF83 0 0 0 0 1 x 0 1 0 0 1 0
0x19448FE7 0 1 1 0 1 x 0 1 0 0 2 0
0xD9B11FB7 0 1 0 3 1 x x x x 0 3 0
0x191C5F97 1 1 0 3 1 x 1 1 0 0 0 0
0x377DAFEF 1 0 1 4 1 x 1 1 0 0 2 0
0x01C00733 0 0 0 x 1 x 0 0 0 0 0 0
0xE8358713 1 0 0 0 1 x 0 1 0 0 0 0
0x06FE0713 0 1 0 0 1 x 0 1 0 0 0 0
0x01A29733 0 0 0 x 1 x 0 0 1 0 0 0
0x00641713 1 1 0 0 1 x 0 1 1 0 0 0
0x41925713 1 1 0 0 1 x 0 1 13 0 0 0
0x0167A733 1 0 0 x 1 x 0 0 2 0 0 0
0xE9B1A713 1 1 0 0 1 x 0 1 2 0 0 0
0x1357A713 1 1 0 0 1 x 0 1 2 0 0 0
0x00DA3733 1 1 0 x 1 x 0 0 3 0 0 0
0xD143B713 1 1 0 0 1 x 0 1 3 0 0 0
0x01E6B713 0 1 0 0 1 x 0 1 3 0 0 0
0x01A74733 0 1 0 x 1 x 0 0 4 0 0 0
0xFEB94713 0 0 0 0 1 x 0 1 4 0 0 0
0x2BF6C713 0 1 0 0 1 x 0 1 4 0 0 0
0x00C0D733 0 1 0 x 1 x 0 0 5 0 0 0
0x00E65713 0 0 0 0 1 x 0 1 5 0 0 0
0x41D95713 1 1 0 0 1 x 0 1 13 0 0 0
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*/
