// Digital circuit RV32I.dig as structural Verilog
module RV32I (
  input  clk,
  output Halt,
  output [31:0] OUT
);

  wire ASel, BrEq, BrLT, BrUn, BSel, MemRW, memWr, outWr, PCSel, RegWEn;
  wire [1:0] WBSel;
  wire [2:0] ImmSel;
  wire [3:0] ALUSel;
  wire [31:0] alu, imm, multiplexer_1_out, multiplexer_2_out, multiplexer_3_out, pc, pc4, RAM_d,
       regfile_1_da, ROM_d, rs2, wb;

  Break #(.Cycles(100000000)) break_1 (.brk(Halt));
  Multiplexer #(.Bits(32)) multiplexer_1 (.sel(PCSel), .in_0(pc4), .in_1({alu[31:1], 1'b0}), .out(multiplexer_1_out));
  Register #(.Bits(32), .isProgramCounter("true")) u_PC (.D(multiplexer_1_out), .C(clk), .en(~Halt), .Q(pc));
  // Probe PC on pc
  Add #(.Bits(32)) add_1 (.a(pc), .b(32'h4), .c_i(1'b0), .s(pc4));  // open: c_o
  ROM #(.AddrBits(12), .isProgramMemory("true"), .Bits(32)) ROM (.A(pc[13:2]), .sel(1'b1), .D(ROM_d));
  // Probe Inst on ROM_d
  Control control_1 (
    .inst(ROM_d), .BrEq(BrEq), .BrLT(BrLT), .PCSel(PCSel), .ImmSel(ImmSel), .RegWEn(RegWEn), .BrUn(BrUn),
    .ASel(ASel), .BSel(BSel), .ALUSel(ALUSel), .MemRW(MemRW), .WBSel(WBSel), .Halt(Halt));
  ImmGen immgen_1 (.inst(ROM_d), .Sel(ImmSel), .imm(imm));
  RegFile regfile_1 (
    .Din(wb), .we(RegWEn), .Rw(ROM_d[11:7]), .C(clk), .Ra(ROM_d[19:15]), .Rb(ROM_d[24:20]),
    .Da(regfile_1_da), .Db(rs2));
  BranchComp branchcomp_1 (.A(regfile_1_da), .B(rs2), .BrUn(BrUn), .BrEq(BrEq), .BrLT(BrLT));
  Multiplexer #(.Bits(32)) multiplexer_2 (.sel(ASel), .in_0(regfile_1_da), .in_1(pc), .out(multiplexer_2_out));
  Multiplexer #(.Bits(32)) multiplexer_3 (.sel(BSel), .in_0(rs2), .in_1(imm), .out(multiplexer_3_out));
  ALU alu_1 (.A(multiplexer_2_out), .B(multiplexer_3_out), .Sel(ALUSel), .R(alu));
  and and_1 (memWr, MemRW, ~alu[31]);  // And
  and and_2 (outWr, alu[31], MemRW);
  // Probe ALU on alu
  RAMDualPort #(.AddrBits(12), .Bits(32)) RAM (.A(alu[13:2]), .Din(rs2), .str(memWr), .C(clk), .ld(1'b1), .D(RAM_d));
  Register #(.Bits(32)) u_OUT (.D(rs2), .C(clk), .en(outWr), .Q(OUT));
  Multiplexer #(.Selector_Bits(2), .Bits(32)) multiplexer_4 (
    .sel(WBSel), .in_0(alu), .in_1(RAM_d), .in_2(pc4), .in_3(imm), .out(wb));
  // Probe WB on wb

  // Notes on the sheet:
  //   clk: Hz: 10
  //   contents of ROM (hex, n*v repeats v):
  //   4137,80000437,493,1800293,513,100593,b4a023,b42023,b50333,58513
  //   ,30593,448493,fff28293,fe0292e3,513,1800593,c000ef,a42023,100073
  //   ,ff810113,112223,1212023,913,259593,a585b3,b57a63,52283,590933
  //   ,450513,ff1ff06f,90513,12903,412083,810113,8067
endmodule

/* Test case Fibonacci:
clk Halt OUT
program(0x4137,0x80000437,0x493,0x1800293,0x513,0x100593,0xB4A023,0xB42023,0xB50333,0x58513,0x30593,0x448493,0xFFF28293,0xFE0292E3,0x513,0x1800593,0xC000EF,0xA42023,0x100073,0xFF810113,0x112223,0x1212023,0x913,0x259593,0xA585B3,0xB57A63,0x52283,0x590933,0x450513,0xFF1FF06F,0x90513,0x12903,0x412083,0x810113,0x8067)
repeat(334) C x x
0 1 0x1DA30
repeat(3) C 1 0x1DA30
*/

/* Test case Selbsttest:
clk Halt OUT
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*/
