// Digital circuit RegFile.dig as structural Verilog
module RegFile (
  input  [31:0] Din,
  input  we,
  input  [4:0] Rw,
  input  C,
  input  [4:0] Ra,
  input  [4:0] Rb,
  output [31:0] Da,
  output [31:0] Db
);

  wire aZero, bZero;
  wire [31:0] Reg_da, Reg_db;

  RegisterFile #(.AddrBits(5), .Bits(32)) Reg (
    .Din(Din), .we(we), .Rw(Rw), .C(C), .Ra(Ra), .Rb(Rb), .Da(Reg_da), .Db(Reg_db));
  Comparator #(.Bits(5)) comparator_1 (.a(Ra), .b({5{1'b0}}), .eq(aZero));  // open: gt, lt
  Comparator #(.Bits(5)) comparator_2 (.a(Rb), .b({5{1'b0}}), .eq(bZero));  // open: gt, lt
  Multiplexer #(.Bits(32)) multiplexer_1 (.sel(bZero), .in_0(Reg_db), .in_1({32{1'b0}}), .out(Db));
  Multiplexer #(.Bits(32)) multiplexer_2 (.sel(aZero), .in_0(Reg_da), .in_1({32{1'b0}}), .out(Da));
endmodule

/* Test case RegFile:
Din we Rw C Ra Rb Da Db
0xDEADBEEF 1 1 C 1 1 0xDEADBEEF 0xDEADBEEF
0x12345678 1 0 C 0 0 0x00000000 0x00000000
0xFFFFFFFF 1 31 C 31 0 0xFFFFFFFF 0x00000000
0x55555555 0 31 C 31 1 0xFFFFFFFF 0xDEADBEEF
0xCAFEBABE 1 0 C 0 31 0x00000000 0xFFFFFFFF
0x00000002 1 2 C 1 2 0xDEADBEEF 0x00000002
0x00000000 0 0 C 2 0 0x00000002 0x00000000
0x00000018 1 3 C 0 3 0x00000000 0x00000018
0x0C981264 1 3 C 0 30 0x00000000 0x00000000
0x00000005 1 0 C 30 1 0x00000000 0xDEADBEEF
0x3F3A7C3F 1 0 C 15 1 0x00000000 0xDEADBEEF
0x22CF109E 0 11 C 1 3 0xDEADBEEF 0x0C981264
0x05F3AEF8 0 30 C 2 0 0x00000002 0x00000000
0x0604F654 1 16 C 1 3 0xDEADBEEF 0x0C981264
0xA63C0EDC 1 1 C 1 31 0xA63C0EDC 0xFFFFFFFF
0x65DFFAE2 0 31 C 27 11 0x00000000 0x00000000
0x00000004 1 31 C 19 3 0x00000000 0x0C981264
0x5BFAC085 0 1 C 31 1 0x00000004 0xA63C0EDC
0xD22B81F7 1 30 C 31 31 0x00000004 0x00000004
0x00000001 1 0 C 31 31 0x00000004 0x00000004
0xFFFFFFF2 1 0 C 0 1 0x00000000 0xA63C0EDC
0xB427F8F3 1 0 C 31 1 0x00000004 0xA63C0EDC
0xF5850D3B 1 16 C 31 3 0x00000004 0x0C981264
0x611BA327 1 3 C 31 0 0x00000004 0x00000000
0xFFFFFFF8 1 1 C 1 2 0xFFFFFFF8 0x00000002
0x90465572 1 3 C 29 2 0x00000000 0x00000002
0x87654321 1 1 C 3 0 0x90465572 0x00000000
0x0000001F 1 0 C 0 31 0x00000000 0x00000004
0x693AEF21 1 31 C 3 31 0x90465572 0x693AEF21
0xE7EBEF75 1 31 C 1 0 0x87654321 0x00000000
0xE909A37B 1 1 C 5 31 0x00000000 0xE7EBEF75
0x0000001D 1 1 C 1 3 0x0000001D 0x90465572
0x8CE8A43B 1 2 C 0 1 0x00000000 0x0000001D
0x0000001C 0 1 C 2 3 0x8CE8A43B 0x90465572
0x198A2543 0 1 C 11 0 0x00000000 0x00000000
0x2E5D3A5A 1 3 C 0 1 0x00000000 0x0000001D
0x00000007 1 1 C 0 1 0x00000000 0x00000007
0xE01690B3 1 30 C 2 2 0x8CE8A43B 0x8CE8A43B
0x113CABF9 1 30 C 2 3 0x8CE8A43B 0x2E5D3A5A
0x48C9DD3F 1 0 C 3 31 0x2E5D3A5A 0xE7EBEF75
0x00000004 1 1 C 0 31 0x00000000 0xE7EBEF75
0xFFFFFFED 1 1 C 31 2 0xE7EBEF75 0x8CE8A43B
0x00000000 1 30 C 3 0 0x2E5D3A5A 0x00000000
0x12345678 1 31 C 3 10 0x2E5D3A5A 0x00000000
0x87654321 1 30 C 1 6 0xFFFFFFED 0x00000000
0x55555555 0 2 C 3 31 0x2E5D3A5A 0x12345678
0xC16B9B72 1 6 C 2 1 0x8CE8A43B 0xFFFFFFED
0x00000001 0 31 C 28 0 0x00000000 0x00000000
0xEE903DEC 1 3 C 1 31 0xFFFFFFED 0x12345678
0x80000001 0 0 C 1 31 0xFFFFFFED 0x12345678
0x6308B5D8 1 1 C 2 1 0x8CE8A43B 0x6308B5D8
0x87654321 1 0 C 3 16 0xEE903DEC 0xF5850D3B
0x00000010 1 3 C 0 2 0x00000000 0x8CE8A43B
0xA59338CB 0 0 C 1 1 0x6308B5D8 0x6308B5D8
0xFFFFFFFA 1 17 C 3 2 0x00000010 0x8CE8A43B
0xF1CB06C6 1 0 C 3 2 0x00000010 0x8CE8A43B
0xFFFFFFFF 1 0 C 4 2 0x00000000 0x8CE8A43B
0x00000013 1 30 C 2 1 0x8CE8A43B 0x6308B5D8
0x00000013 1 0 C 4 3 0x00000000 0x00000010
0xC37560F7 0 0 C 3 1 0x00000010 0x6308B5D8
0x5C3985E3 1 2 C 1 2 0x6308B5D8 0x5C3985E3
0x00000011 1 30 C 0 13 0x00000000 0x00000000
0x44DF5D46 1 3 C 0 0 0x00000000 0x00000000
0x0000000F 1 31 C 0 31 0x00000000 0x0000000F
0xFFFF0000 1 9 C 6 1 0xC16B9B72 0x6308B5D8
0x00000014 1 0 C 0 3 0x00000000 0x44DF5D46
0x00000008 0 0 C 3 21 0x44DF5D46 0x00000000
0x00000001 0 0 C 31 31 0x0000000F 0x0000000F
0xC0ACDC73 0 1 C 2 31 0x5C3985E3 0x0000000F
0x00000021 1 0 C 1 3 0x6308B5D8 0x44DF5D46
0x87654321 1 0 C 1 3 0x6308B5D8 0x44DF5D46
0xB8D0D0C0 1 31 C 3 0 0x44DF5D46 0x00000000
0x00000004 1 0 C 1 0 0x6308B5D8 0x00000000
0xFFFFFFFF 1 30 C 2 31 0x5C3985E3 0xB8D0D0C0
0x7C9865C5 1 0 C 19 2 0x00000000 0x5C3985E3
0x2C199E88 1 30 C 0 3 0x00000000 0x44DF5D46
0xFFFFFFF4 0 0 C 1 3 0x6308B5D8 0x44DF5D46
0xFFFFFFEE 1 31 C 1 2 0x6308B5D8 0x5C3985E3
0xFFFFFFFD 0 1 C 3 0 0x44DF5D46 0x00000000
0xD88B167A 1 1 C 23 1 0x00000000 0xD88B167A
0xFFB1C29A 0 3 C 0 25 0x00000000 0x00000000
0x00000020 1 0 C 31 31 0xFFFFFFEE 0xFFFFFFEE
0x00000021 1 2 C 17 2 0xFFFFFFFA 0x00000021
0x00000000 1 31 C 1 1 0xD88B167A 0xD88B167A
0x00000000 1 2 C 1 1 0xD88B167A 0xD88B167A
0x0000000C 1 3 C 31 1 0x00000000 0xD88B167A
0xFFFFFFFF 1 0 C 1 1 0xD88B167A 0xD88B167A
0xF6B0C1FF 0 3 C 3 26 0x0000000C 0x00000000
0xDD4616DE 1 0 C 6 31 0xC16B9B72 0x00000000
0x00000000 1 0 C 16 2 0xF5850D3B 0x00000000
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*/
