// Digital circuit ShiftLeft.dig as structural Verilog
module ShiftLeft (
  input  [31:0] in,
  input  [4:0] shamt,
  output [31:0] out
);

  wire [31:0] multiplexer_1_out, multiplexer_2_out, multiplexer_3_out, multiplexer_4_out;

  Multiplexer #(.Bits(32)) multiplexer_1 (.sel(shamt[0]), .in_0(in), .in_1({in[30:0], 1'b0}), .out(multiplexer_1_out));
  Multiplexer #(.Bits(32)) multiplexer_2 (
    .sel(shamt[1]), .in_0(multiplexer_1_out), .in_1({multiplexer_1_out[29:0], 2'b00}), .out(multiplexer_2_out));
  Multiplexer #(.Bits(32)) multiplexer_3 (
    .sel(shamt[2]), .in_0(multiplexer_2_out), .in_1({multiplexer_2_out[27:0], 4'b0000}),
    .out(multiplexer_3_out));
  Multiplexer #(.Bits(32)) multiplexer_4 (
    .sel(shamt[3]), .in_0(multiplexer_3_out), .in_1({multiplexer_3_out[23:0], {8{1'b0}}}),
    .out(multiplexer_4_out));
  Multiplexer #(.Bits(32)) multiplexer_5 (
    .sel(shamt[4]), .in_0(multiplexer_4_out), .in_1({multiplexer_4_out[15:0], {16{1'b0}}}), .out(out));
endmodule

/* Test case ShiftLeft:
in shamt out
0x00000000 0 0x00000000
0x00000000 1 0x00000000
0x00000000 2 0x00000000
0x00000000 3 0x00000000
0x00000000 4 0x00000000
0x00000000 7 0x00000000
0x00000000 8 0x00000000
0x00000000 15 0x00000000
0x00000000 16 0x00000000
0x00000000 17 0x00000000
0x00000000 30 0x00000000
0x00000000 31 0x00000000
0x00000000 6 0x00000000
0x00000000 2 0x00000000
0x00000000 18 0x00000000
0x00000000 19 0x00000000
0x00000001 0 0x00000001
0x00000001 1 0x00000002
0x00000001 2 0x00000004
0x00000001 3 0x00000008
0x00000001 4 0x00000010
0x00000001 7 0x00000080
0x00000001 8 0x00000100
0x00000001 15 0x00008000
0x00000001 16 0x00010000
0x00000001 17 0x00020000
0x00000001 30 0x40000000
0x00000001 31 0x80000000
0x00000001 27 0x08000000
0x00000001 27 0x08000000
0x00000001 19 0x00080000
0x00000001 30 0x40000000
0x80000000 0 0x80000000
0x80000000 1 0x00000000
0x80000000 2 0x00000000
0x80000000 3 0x00000000
0x80000000 4 0x00000000
0x80000000 7 0x00000000
0x80000000 8 0x00000000
0x80000000 15 0x00000000
0x80000000 16 0x00000000
0x80000000 17 0x00000000
0x80000000 30 0x00000000
0x80000000 31 0x00000000
0x80000000 20 0x00000000
0x80000000 25 0x00000000
0x80000000 21 0x00000000
0x80000000 9 0x00000000
0xFFFFFFFF 0 0xFFFFFFFF
0xFFFFFFFF 1 0xFFFFFFFE
0xFFFFFFFF 2 0xFFFFFFFC
0xFFFFFFFF 3 0xFFFFFFF8
0xFFFFFFFF 4 0xFFFFFFF0
0xFFFFFFFF 7 0xFFFFFF80
0xFFFFFFFF 8 0xFFFFFF00
0xFFFFFFFF 15 0xFFFF8000
0xFFFFFFFF 16 0xFFFF0000
0xFFFFFFFF 17 0xFFFE0000
0xFFFFFFFF 30 0xC0000000
0xFFFFFFFF 31 0x80000000
0xFFFFFFFF 8 0xFFFFFF00
0xFFFFFFFF 6 0xFFFFFFC0
0xFFFFFFFF 12 0xFFFFF000
0xFFFFFFFF 31 0x80000000
0x7FFFFFFF 0 0x7FFFFFFF
0x7FFFFFFF 1 0xFFFFFFFE
0x7FFFFFFF 2 0xFFFFFFFC
0x7FFFFFFF 3 0xFFFFFFF8
0x7FFFFFFF 4 0xFFFFFFF0
0x7FFFFFFF 7 0xFFFFFF80
0x7FFFFFFF 8 0xFFFFFF00
0x7FFFFFFF 15 0xFFFF8000
0x7FFFFFFF 16 0xFFFF0000
0x7FFFFFFF 17 0xFFFE0000
0x7FFFFFFF 30 0xC0000000
0x7FFFFFFF 31 0x80000000
0x7FFFFFFF 18 0xFFFC0000
0x7FFFFFFF 15 0xFFFF8000
0x7FFFFFFF 20 0xFFF00000
0x7FFFFFFF 31 0x80000000
0x12345678 0 0x12345678
0x12345678 1 0x2468ACF0
0x12345678 2 0x48D159E0
0x12345678 3 0x91A2B3C0
0x12345678 4 0x23456780
0x12345678 7 0x1A2B3C00
0x12345678 8 0x34567800
0x12345678 15 0x2B3C0000
0x12345678 16 0x56780000
0x12345678 17 0xACF00000
0x12345678 30 0x00000000
0x12345678 31 0x00000000
0x12345678 29 0x00000000
0x12345678 1 0x2468ACF0
0x12345678 8 0x34567800
0x12345678 17 0xACF00000
0x87654321 0 0x87654321
0x87654321 1 0x0ECA8642
0x87654321 2 0x1D950C84
0x87654321 3 0x3B2A1908
0x87654321 4 0x76543210
0x87654321 7 0xB2A19080
0x87654321 8 0x65432100
0x87654321 15 0xA1908000
0x87654321 16 0x43210000
0x87654321 17 0x86420000
0x87654321 30 0x40000000
0x87654321 31 0x80000000
0x87654321 13 0xA8642000
0x87654321 14 0x50C84000
0x87654321 15 0xA1908000
0x87654321 9 0xCA864200
0xAAAAAAAA 0 0xAAAAAAAA
0xAAAAAAAA 1 0x55555554
0xAAAAAAAA 2 0xAAAAAAA8
0xAAAAAAAA 3 0x55555550
0xAAAAAAAA 4 0xAAAAAAA0
0xAAAAAAAA 7 0x55555500
0xAAAAAAAA 8 0xAAAAAA00
0xAAAAAAAA 15 0x55550000
0xAAAAAAAA 16 0xAAAA0000
0xAAAAAAAA 17 0x55540000
0xAAAAAAAA 30 0x80000000
0xAAAAAAAA 31 0x00000000
0xAAAAAAAA 30 0x80000000
0xAAAAAAAA 30 0x80000000
0xAAAAAAAA 9 0x55555400
0xAAAAAAAA 11 0x55555000
0x55555555 0 0x55555555
0x55555555 1 0xAAAAAAAA
0x55555555 2 0x55555554
0x55555555 3 0xAAAAAAA8
0x55555555 4 0x55555550
0x55555555 7 0xAAAAAA80
0x55555555 8 0x55555500
0x55555555 15 0xAAAA8000
0x55555555 16 0x55550000
0x55555555 17 0xAAAA0000
0x55555555 30 0x40000000
0x55555555 31 0x80000000
0x55555555 0 0x55555555
0x55555555 10 0x55555400
0x55555555 0 0x55555555
0x55555555 11 0xAAAAA800
0x384735EE 0 0x384735EE
0x384735EE 1 0x708E6BDC
0x384735EE 2 0xE11CD7B8
0x384735EE 3 0xC239AF70
0x384735EE 4 0x84735EE0
0x384735EE 7 0x239AF700
0x384735EE 8 0x4735EE00
0x384735EE 15 0x9AF70000
0x384735EE 16 0x35EE0000
0x384735EE 17 0x6BDC0000
0x384735EE 30 0x80000000
0x384735EE 31 0x00000000
0x384735EE 11 0x39AF7000
0x384735EE 9 0x8E6BDC00
0x384735EE 22 0x7B800000
0x384735EE 10 0x1CD7B800
0x2EDECF68 0 0x2EDECF68
0x2EDECF68 1 0x5DBD9ED0
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*/
