// Digital circuit ShiftRight.dig as structural Verilog
module ShiftRight (
  input  [31:0] in,
  input  [4:0] shamt,
  input  arith,
  output [31:0] out
);

  wire fill;
  wire [1:0] bitextender_1_out;
  wire [3:0] bitextender_2_out;
  wire [7:0] bitextender_3_out;
  wire [15:0] bitextender_4_out;
  wire [31:0] multiplexer_1_out, multiplexer_2_out, multiplexer_3_out, multiplexer_4_out;

  and and_1 (fill, in[31], arith);
  Multiplexer #(.Bits(32)) multiplexer_1 (.sel(shamt[0]), .in_0(in), .in_1({fill, in[31:1]}), .out(multiplexer_1_out));
  BitExtender #(.inputBits(1), .outputBits(2)) bitextender_1 (.in(fill), .out(bitextender_1_out));
  Multiplexer #(.Bits(32)) multiplexer_2 (
    .sel(shamt[1]), .in_0(multiplexer_1_out), .in_1({bitextender_1_out, multiplexer_1_out[31:2]}),
    .out(multiplexer_2_out));
  BitExtender #(.inputBits(1), .outputBits(4)) bitextender_2 (.in(fill), .out(bitextender_2_out));
  Multiplexer #(.Bits(32)) multiplexer_3 (
    .sel(shamt[2]), .in_0(multiplexer_2_out), .in_1({bitextender_2_out, multiplexer_2_out[31:4]}),
    .out(multiplexer_3_out));
  BitExtender #(.inputBits(1), .outputBits(8)) bitextender_3 (.in(fill), .out(bitextender_3_out));
  Multiplexer #(.Bits(32)) multiplexer_4 (
    .sel(shamt[3]), .in_0(multiplexer_3_out), .in_1({bitextender_3_out, multiplexer_3_out[31:8]}),
    .out(multiplexer_4_out));
  BitExtender #(.inputBits(1)) bitextender_4 (.in(fill), .out(bitextender_4_out));
  Multiplexer #(.Bits(32)) multiplexer_5 (
    .sel(shamt[4]), .in_0(multiplexer_4_out), .in_1({bitextender_4_out, multiplexer_4_out[31:16]}), .out(out));
endmodule

/* Test case ShiftRight:
in shamt arith out
0x00000000 0 0 0x00000000
0x00000000 0 1 0x00000000
0x00000000 1 0 0x00000000
0x00000000 1 1 0x00000000
0x00000000 2 0 0x00000000
0x00000000 2 1 0x00000000
0x00000000 3 0 0x00000000
0x00000000 3 1 0x00000000
0x00000000 4 0 0x00000000
0x00000000 4 1 0x00000000
0x00000000 7 0 0x00000000
0x00000000 7 1 0x00000000
0x00000000 8 0 0x00000000
0x00000000 8 1 0x00000000
0x00000000 15 0 0x00000000
0x00000000 15 1 0x00000000
0x00000000 16 0 0x00000000
0x00000000 16 1 0x00000000
0x00000000 17 0 0x00000000
0x00000000 17 1 0x00000000
0x00000000 30 0 0x00000000
0x00000000 30 1 0x00000000
0x00000000 31 0 0x00000000
0x00000000 31 1 0x00000000
0x00000000 6 0 0x00000000
0x00000000 6 1 0x00000000
0x00000000 2 0 0x00000000
0x00000000 2 1 0x00000000
0x00000000 18 0 0x00000000
0x00000000 18 1 0x00000000
0x00000000 19 0 0x00000000
0x00000000 19 1 0x00000000
0x00000001 0 0 0x00000001
0x00000001 0 1 0x00000001
0x00000001 1 0 0x00000000
0x00000001 1 1 0x00000000
0x00000001 2 0 0x00000000
0x00000001 2 1 0x00000000
0x00000001 3 0 0x00000000
0x00000001 3 1 0x00000000
0x00000001 4 0 0x00000000
0x00000001 4 1 0x00000000
0x00000001 7 0 0x00000000
0x00000001 7 1 0x00000000
0x00000001 8 0 0x00000000
0x00000001 8 1 0x00000000
0x00000001 15 0 0x00000000
0x00000001 15 1 0x00000000
0x00000001 16 0 0x00000000
0x00000001 16 1 0x00000000
0x00000001 17 0 0x00000000
0x00000001 17 1 0x00000000
0x00000001 30 0 0x00000000
0x00000001 30 1 0x00000000
0x00000001 31 0 0x00000000
0x00000001 31 1 0x00000000
0x00000001 27 0 0x00000000
0x00000001 27 1 0x00000000
0x00000001 27 0 0x00000000
0x00000001 27 1 0x00000000
0x00000001 19 0 0x00000000
0x00000001 19 1 0x00000000
0x00000001 30 0 0x00000000
0x00000001 30 1 0x00000000
0x80000000 0 0 0x80000000
0x80000000 0 1 0x80000000
0x80000000 1 0 0x40000000
0x80000000 1 1 0xC0000000
0x80000000 2 0 0x20000000
0x80000000 2 1 0xE0000000
0x80000000 3 0 0x10000000
0x80000000 3 1 0xF0000000
0x80000000 4 0 0x08000000
0x80000000 4 1 0xF8000000
0x80000000 7 0 0x01000000
0x80000000 7 1 0xFF000000
0x80000000 8 0 0x00800000
0x80000000 8 1 0xFF800000
0x80000000 15 0 0x00010000
0x80000000 15 1 0xFFFF0000
0x80000000 16 0 0x00008000
0x80000000 16 1 0xFFFF8000
0x80000000 17 0 0x00004000
0x80000000 17 1 0xFFFFC000
0x80000000 30 0 0x00000002
0x80000000 30 1 0xFFFFFFFE
0x80000000 31 0 0x00000001
0x80000000 31 1 0xFFFFFFFF
0x80000000 20 0 0x00000800
0x80000000 20 1 0xFFFFF800
0x80000000 25 0 0x00000040
0x80000000 25 1 0xFFFFFFC0
0x80000000 21 0 0x00000400
0x80000000 21 1 0xFFFFFC00
0x80000000 9 0 0x00400000
0x80000000 9 1 0xFFC00000
0xFFFFFFFF 0 0 0xFFFFFFFF
0xFFFFFFFF 0 1 0xFFFFFFFF
0xFFFFFFFF 1 0 0x7FFFFFFF
0xFFFFFFFF 1 1 0xFFFFFFFF
0xFFFFFFFF 2 0 0x3FFFFFFF
0xFFFFFFFF 2 1 0xFFFFFFFF
0xFFFFFFFF 3 0 0x1FFFFFFF
0xFFFFFFFF 3 1 0xFFFFFFFF
0xFFFFFFFF 4 0 0x0FFFFFFF
0xFFFFFFFF 4 1 0xFFFFFFFF
0xFFFFFFFF 7 0 0x01FFFFFF
0xFFFFFFFF 7 1 0xFFFFFFFF
0xFFFFFFFF 8 0 0x00FFFFFF
0xFFFFFFFF 8 1 0xFFFFFFFF
0xFFFFFFFF 15 0 0x0001FFFF
0xFFFFFFFF 15 1 0xFFFFFFFF
0xFFFFFFFF 16 0 0x0000FFFF
0xFFFFFFFF 16 1 0xFFFFFFFF
0xFFFFFFFF 17 0 0x00007FFF
0xFFFFFFFF 17 1 0xFFFFFFFF
0xFFFFFFFF 30 0 0x00000003
0xFFFFFFFF 30 1 0xFFFFFFFF
0xFFFFFFFF 31 0 0x00000001
0xFFFFFFFF 31 1 0xFFFFFFFF
0xFFFFFFFF 8 0 0x00FFFFFF
0xFFFFFFFF 8 1 0xFFFFFFFF
0xFFFFFFFF 6 0 0x03FFFFFF
0xFFFFFFFF 6 1 0xFFFFFFFF
0xFFFFFFFF 12 0 0x000FFFFF
0xFFFFFFFF 12 1 0xFFFFFFFF
0xFFFFFFFF 31 0 0x00000001
0xFFFFFFFF 31 1 0xFFFFFFFF
0x7FFFFFFF 0 0 0x7FFFFFFF
0x7FFFFFFF 0 1 0x7FFFFFFF
0x7FFFFFFF 1 0 0x3FFFFFFF
0x7FFFFFFF 1 1 0x3FFFFFFF
0x7FFFFFFF 2 0 0x1FFFFFFF
0x7FFFFFFF 2 1 0x1FFFFFFF
0x7FFFFFFF 3 0 0x0FFFFFFF
0x7FFFFFFF 3 1 0x0FFFFFFF
0x7FFFFFFF 4 0 0x07FFFFFF
0x7FFFFFFF 4 1 0x07FFFFFF
0x7FFFFFFF 7 0 0x00FFFFFF
0x7FFFFFFF 7 1 0x00FFFFFF
0x7FFFFFFF 8 0 0x007FFFFF
0x7FFFFFFF 8 1 0x007FFFFF
0x7FFFFFFF 15 0 0x0000FFFF
0x7FFFFFFF 15 1 0x0000FFFF
0x7FFFFFFF 16 0 0x00007FFF
0x7FFFFFFF 16 1 0x00007FFF
0x7FFFFFFF 17 0 0x00003FFF
0x7FFFFFFF 17 1 0x00003FFF
0x7FFFFFFF 30 0 0x00000001
0x7FFFFFFF 30 1 0x00000001
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*/
